// Logisim project ALU.circ as structural Verilog: 1 circuit, main circuit main
module main (
  input  [15:0] A,
  input  [15:0] B,
  input  [2:0] ALUControl,
  output [15:0] ALUOutput,
  output Negative,
  output Zero
);

  wire [15:0] adder_1_out, and_1_out, divider_1_out, multiplier_1_out, not_1_out, or_1_out, subtractor_1_out;

  Adder #(.width(16)) adder_1 (.a(A), .b(B), .out(adder_1_out), .cin(1'b0));  // open: cout
  Subtractor #(.width(16)) subtractor_1 (.a(A), .b(B), .out(subtractor_1_out), .bin(1'b0));  // open: bout
  Multiplier #(.width(16)) multiplier_1 (.a(A), .b(B), .out(multiplier_1_out), .cin({16{1'b0}}));  // open: cout
  Divider #(.width(16)) divider_1 (.a(A), .b(B), .out(divider_1_out), .upper({16{1'b0}}));  // open: rem
  assign not_1_out = ~A;  // NOT_Gate not_1, 16 bits wide
  assign and_1_out = A & B;  // AND_Gate and_1, 16 bits wide
  assign or_1_out = A | B;  // OR_Gate or_1, 16 bits wide
  Multiplexer #(.select(3), .width(16), .enable("false")) multiplexer_1 (
    .in0(adder_1_out), .in1(subtractor_1_out), .in2(multiplier_1_out), .in3(divider_1_out), .in4(and_1_out),
    .in5(or_1_out), .in6(not_1_out), .out(ALUOutput), .sel(ALUControl));  // open: in7
  nor nor_1 (Zero, ALUOutput[15], ALUOutput[14], ALUOutput[13], ALUOutput[12], ALUOutput[11], ALUOutput[10], ALUOutput[9], ALUOutput[8], ALUOutput[7], ALUOutput[6], ALUOutput[5], ALUOutput[4], ALUOutput[3], ALUOutput[2], ALUOutput[1], ALUOutput[0]);

  assign Negative = ALUOutput[15];
endmodule
