// Logisim project Control-Unit.circ as structural Verilog: 4 circuits, main circuit main
module main (
  input  [2:0] Op,
  input  [1:0] Type,
  output out_3,
  output out_4,
  output out_5,
  output out_6,
  output out_7,
  output out_8,
  output out_9,
  output out_10,
  output out_11,
  output out_12,
  output out_13,
  output out_14
);

  wire [11:0] a_type_1_alucontrol2, b_type_1_alucontrol0, c_type_1_alucontrol2;

  A_type a_type_1 (
    .Op0(Op[2]), .Op1(Op[1]), .Op2(Op[0]), .ALUControl0(a_type_1_alucontrol2[2]),
    .ALUControl1(a_type_1_alucontrol2[1]), .ALUControl2(a_type_1_alucontrol2[0]),
    .BrControl(a_type_1_alucontrol2[3]), .JmpControl(a_type_1_alucontrol2[4]),
    .RegWrite(a_type_1_alucontrol2[5]), .MemWrite(a_type_1_alucontrol2[6]),
    .BrSelect0(a_type_1_alucontrol2[8]), .BrSelect1(a_type_1_alucontrol2[7]),
    .A3Select(a_type_1_alucontrol2[9]), .WD3Select0(a_type_1_alucontrol2[11]),
    .WD3Select1(a_type_1_alucontrol2[10]));
  B_type b_type_1 (
    .Op1(Op[1]), .Op0(Op[0]), .ALUControl2(b_type_1_alucontrol0[2]), .ALUControl1(b_type_1_alucontrol0[1]),
    .ALUControl0(b_type_1_alucontrol0[0]), .BrControl(b_type_1_alucontrol0[3]),
    .JmpControl(b_type_1_alucontrol0[4]), .RegWrite(b_type_1_alucontrol0[5]),
    .MemWrite(b_type_1_alucontrol0[6]), .BrSelect1(b_type_1_alucontrol0[8]),
    .BrSelect0(b_type_1_alucontrol0[7]), .A3Select(b_type_1_alucontrol0[9]),
    .WD3Select1(b_type_1_alucontrol0[11]), .WD3Select0(b_type_1_alucontrol0[10]));
  C_type c_type_1 (
    .Op1(Op[1]), .Op2(Op[0]), .ALUControl0(c_type_1_alucontrol2[2]), .ALUControl1(c_type_1_alucontrol2[1]),
    .ALUControl2(c_type_1_alucontrol2[0]), .BrControl(c_type_1_alucontrol2[3]),
    .JmpControl(c_type_1_alucontrol2[4]), .RegWrite(c_type_1_alucontrol2[5]),
    .MemWrite(c_type_1_alucontrol2[6]), .BrSelect0(c_type_1_alucontrol2[8]),
    .BrSelect1(c_type_1_alucontrol2[7]), .A3Select(c_type_1_alucontrol2[9]),
    .WD3Select0(c_type_1_alucontrol2[11]), .WD3Select1(c_type_1_alucontrol2[10]));
  Multiplexer #(.select(2), .width(12), .enable("false")) multiplexer_1 (
    .in0(a_type_1_alucontrol2), .in1(b_type_1_alucontrol0), .in2(c_type_1_alucontrol2),
    .out({out_14, out_13, out_12, out_11, out_10, out_9, out_8, out_7, out_6, out_5, out_4, out_3}),
    .sel(Type));  // open: in3
endmodule

module A_type (
  input  Op0,
  input  Op1,
  input  Op2,
  output ALUControl0,
  output ALUControl1,
  output ALUControl2,
  output BrControl,
  output JmpControl,
  output RegWrite,
  output MemWrite,
  output BrSelect0,
  output BrSelect1,
  output A3Select,
  output WD3Select0,
  output WD3Select1
);


  assign A3Select = 1'b0;
  assign ALUControl0 = Op0;
  assign ALUControl1 = Op1;
  assign ALUControl2 = Op2;
  assign BrControl = 1'b0;
  assign JmpControl = 1'b0;
  assign MemWrite = 1'b0;
  assign RegWrite = 1'b1;
  assign WD3Select0 = 1'b0;
  assign WD3Select1 = 1'b0;
endmodule

module B_type (
  input  Op1,
  input  Op0,
  output ALUControl2,
  output ALUControl1,
  output ALUControl0,
  output BrControl,
  output JmpControl,
  output RegWrite,
  output MemWrite,
  output BrSelect1,
  output BrSelect0,
  output A3Select,
  output WD3Select1,
  output WD3Select0
);


  assign ALUControl0 = 1'b1;
  assign ALUControl1 = 1'b0;
  assign ALUControl2 = 1'b0;
  assign BrControl = 1'b1;
  assign BrSelect0 = Op0;
  assign BrSelect1 = Op1;
  assign JmpControl = 1'b0;
  assign MemWrite = 1'b0;
  assign RegWrite = 1'b0;
endmodule

module C_type (
  input  Op1,
  input  Op2,
  output ALUControl0,
  output ALUControl1,
  output ALUControl2,
  output BrControl,
  output JmpControl,
  output RegWrite,
  output MemWrite,
  output BrSelect0,
  output BrSelect1,
  output A3Select,
  output WD3Select0,
  output WD3Select1
);

  wire and_3_out, and_4_out, not_1_out, not_2_out, not_3_out, not_4_out;

  not not_1 (not_1_out, Op1);
  not not_2 (not_2_out, Op2);
  not not_3 (not_3_out, Op1);
  not not_4 (not_4_out, Op2);
  and and_1 (MemWrite, Op1, Op2);
  not not_5 (WD3Select0, Op2);
  not not_6 (WD3Select1, Op1);
  and and_2 (JmpControl, not_1_out, not_2_out);
  and and_3 (and_3_out, not_3_out, Op2);
  and and_4 (and_4_out, Op1, not_4_out);
  or or_1 (RegWrite, and_3_out, and_4_out);

  assign A3Select = 1'b1;
  assign BrControl = 1'b0;
endmodule
