// Logisim project GROUP-13-MICROPROCESSORS-REGISTERFILE.circ as structural Verilog
module _16_Bit_RegisterFile (
  input  [3:0] Write_Register,
  input  [3:0] readRegister_2,
  input  [3:0] readRegister_1,
  input  [15:0] Write_Data,
  input  RegWrite,
  output [15:0] read_data_1,
  output [15:0] read_data_2
);

  wire and_1_out, and_2_out, and_3_out, and_4_out, and_5_out, and_6_out, and_7_out, and_8_out, and_9_out,
       and_10_out, and_11_out, and_12_out, and_13_out, and_14_out, and_15_out, and_16_out, Clock_out,
       decoder_1_out0, decoder_1_out1, decoder_1_out2, decoder_1_out3, decoder_1_out4, decoder_1_out5,
       decoder_1_out6, decoder_1_out7, decoder_1_out8, decoder_1_out9, decoder_1_out10, decoder_1_out11,
       decoder_1_out12, decoder_1_out13, decoder_1_out14, decoder_1_out15;
  wire [15:0] register_1_q, register_2_q, register_3_q, register_4_q, register_5_q, register_6_q,
       register_7_q, register_8_q, register_9_q, register_10_q, register_11_q, register_12_q, register_13_q,
       register_14_q, register_15_q, register_16_q;

  Decoder #(.select(4)) decoder_1 (
    .out0(decoder_1_out0), .out1(decoder_1_out1), .out2(decoder_1_out2), .out3(decoder_1_out3),
    .out4(decoder_1_out4), .out5(decoder_1_out5), .out6(decoder_1_out6), .out7(decoder_1_out7),
    .out8(decoder_1_out8), .out9(decoder_1_out9), .out10(decoder_1_out10), .out11(decoder_1_out11),
    .out12(decoder_1_out12), .out13(decoder_1_out13), .out14(decoder_1_out14), .out15(decoder_1_out15),
    .sel(Write_Register));  // open: en
  and and_1 (and_1_out, decoder_1_out0, RegWrite);
  and and_2 (and_2_out, decoder_1_out1, RegWrite);
  and and_3 (and_3_out, decoder_1_out2, RegWrite);
  and and_4 (and_4_out, decoder_1_out3, RegWrite);
  and and_5 (and_5_out, decoder_1_out4, RegWrite);
  and and_6 (and_6_out, decoder_1_out5, RegWrite);
  and and_7 (and_7_out, decoder_1_out6, RegWrite);
  and and_8 (and_8_out, decoder_1_out7, RegWrite);
  Clock Clock (.out(Clock_out));
  Register #(.width(16)) register_1 (.D(Write_Data), .Q(register_1_q), .clk(Clock_out), .clr(and_1_out));  // open: en
  Register #(.width(16)) register_2 (.D(Write_Data), .Q(register_2_q), .clk(Clock_out), .clr(and_2_out));  // open: en
  Register #(.width(16)) register_3 (.D(Write_Data), .Q(register_3_q), .clk(Clock_out), .clr(and_3_out));  // open: en
  Register #(.width(16)) register_4 (.D(Write_Data), .Q(register_4_q), .clk(Clock_out), .clr(and_4_out));  // open: en
  Register #(.width(16)) register_5 (.D(Write_Data), .Q(register_5_q), .clk(Clock_out), .clr(and_5_out));  // open: en
  Register #(.width(16)) register_6 (.D(Write_Data), .Q(register_6_q), .clk(Clock_out), .clr(and_6_out));  // open: en
  Register #(.width(16)) register_7 (.D(Write_Data), .Q(register_7_q), .clk(Clock_out), .clr(and_7_out));  // open: en
  Register #(.width(16)) register_8 (.D(Write_Data), .Q(register_8_q), .clk(Clock_out), .clr(and_8_out));  // open: en
  and and_9 (and_9_out, decoder_1_out8, RegWrite);
  and and_10 (and_10_out, decoder_1_out9, RegWrite);
  and and_11 (and_11_out, decoder_1_out10, RegWrite);
  and and_12 (and_12_out, decoder_1_out11, RegWrite);
  and and_13 (and_13_out, decoder_1_out12, RegWrite);
  and and_14 (and_14_out, decoder_1_out13, RegWrite);
  and and_15 (and_15_out, decoder_1_out14, RegWrite);
  and and_16 (and_16_out, decoder_1_out15, RegWrite);
  Register #(.width(16)) register_9 (.D(Write_Data), .Q(register_9_q), .clk(Clock_out), .clr(and_9_out));  // open: en
  Register #(.width(16)) register_10 (
    .D(Write_Data), .Q(register_10_q), .clk(Clock_out), .clr(and_10_out));  // open: en
  Register #(.width(16)) register_11 (
    .D(Write_Data), .Q(register_11_q), .clk(Clock_out), .clr(and_11_out));  // open: en
  Register #(.width(16)) register_12 (
    .D(Write_Data), .Q(register_12_q), .clk(Clock_out), .clr(and_12_out));  // open: en
  Register #(.width(16)) register_13 (
    .D(Write_Data), .Q(register_13_q), .clk(Clock_out), .clr(and_13_out));  // open: en
  Register #(.width(16)) register_14 (
    .D(Write_Data), .Q(register_14_q), .clk(Clock_out), .clr(and_14_out));  // open: en
  Register #(.width(16)) register_15 (
    .D(Write_Data), .Q(register_15_q), .clk(Clock_out), .clr(and_15_out));  // open: en
  Register #(.width(16)) register_16 (
    .D(Write_Data), .Q(register_16_q), .clk(Clock_out), .clr(and_16_out));  // open: en
  Multiplexer #(.select(4), .width(16)) multiplexer_1 (
    .in0(register_1_q), .in1(register_2_q), .in2(register_3_q), .in3(register_4_q), .in4(register_5_q),
    .in5(register_6_q), .in6(register_7_q), .in7(register_8_q), .in8(register_9_q), .in9(register_10_q),
    .in10(register_11_q), .in11(register_12_q), .in12(register_13_q), .in13(register_14_q),
    .in14(register_15_q), .in15(register_16_q), .out(read_data_1), .sel(readRegister_1));  // open: en
  Multiplexer #(.select(4), .width(16)) multiplexer_2 (
    .in0(register_1_q), .in1(register_2_q), .in2(register_3_q), .in3(register_4_q), .in4(register_5_q),
    .in5(register_6_q), .in6(register_7_q), .in7(register_8_q), .in8(register_9_q), .in9(register_10_q),
    .in10(register_11_q), .in11(register_12_q), .in12(register_13_q), .in13(register_14_q),
    .in14(register_15_q), .in15(register_16_q), .out(read_data_2), .sel(readRegister_2));  // open: en
endmodule
