// Logisim project Project-Microarchitecture.circ as structural Verilog: 1 circuit, main circuit main
module main (
  input  in_1,
  input  in_2
);

  wire A3Select, and_1_out, BrControl, CLK, JmpControl, main_3_negative, main_3_zero, MemWrite,
       multiplexer_6_out, not_1_out, not_2_out, RegWrite;
  wire [1:0] BrSelect, WD3Select;
  wire [2:0] ALUControl, rom_1_data_2;
  wire [3:0] multiplexer_2_out;
  wire [15:0] adder_1_out, adder_2_out, bit_extender_1_out, main_2_rd1, main_2_rd2, main_3_aluoutput,
       multiplexer_1_out, multiplexer_3_out, multiplexer_4_out, multiplexer_5_out, PC_q, ram_1_data,
       rom_1_data;
  wire [25:3] rom_1_data_3;

  Adder #(.width(16)) adder_1 (.a(PC_q), .b(16'h1), .out(adder_1_out), .cin(1'b0));  // open: cout
  Multiplexer #(.width(16), .enable("false")) multiplexer_1 (
    .in0(adder_1_out), .in1(rom_1_data), .out(multiplexer_1_out), .sel(JmpControl));
  Register #(.width(16)) PC (.D(multiplexer_3_out), .en(1'b1), .Q(PC_q), .clk(CLK), .clr(in_1));
  ROM #(.addrWidth(16), .dataWidth(26)) rom_1 (
    .addr(PC_q), .data({rom_1_data_3[25:20], rom_1_data, rom_1_data_3[3], rom_1_data_2}), .sel(1'b1));
  Clock u_CLK (.out(CLK));
  Control_Unit_main main_1 (
    .Op(rom_1_data_2), .out_3(ALUControl[0]), .out_4(ALUControl[1]), .out_5(ALUControl[2]),
    .out_6(BrControl), .out_7(JmpControl), .out_8(RegWrite), .out_9(MemWrite), .out_10(BrSelect[0]),
    .out_11(BrSelect[1]), .out_12(A3Select), .out_13(WD3Select[0]), .out_14(WD3Select[1]),
    .Type(rom_1_data_3[25:24]));
  assign bit_extender_1_out = {{4{rom_1_data[11]}}, rom_1_data[11:0]};  // Bit_Extender bit_extender_1
  Multiplexer #(.width(4), .enable("false")) multiplexer_2 (
    .in0(rom_1_data[11:8]), .in1(rom_1_data_3[23:20]), .out(multiplexer_2_out), .sel(A3Select));
  Multiplexer #(.width(16), .enable("false")) multiplexer_3 (
    .in0(multiplexer_1_out), .in1(multiplexer_4_out), .out(multiplexer_3_out), .sel(BrControl));
  Adder #(.width(16)) adder_2 (
    .a(multiplexer_1_out), .b(bit_extender_1_out), .out(adder_2_out), .cin(1'b0));  // open: cout
  Multiplexer #(.width(16), .enable("false")) multiplexer_4 (
    .in0(multiplexer_1_out), .in1(adder_2_out), .out(multiplexer_4_out), .sel(multiplexer_6_out));
  Registerfile_main main_2 (
    .A3(multiplexer_2_out), .A2(rom_1_data[15:12]), .A1(rom_1_data_3[23:20]), .WD3(multiplexer_5_out),
    .RD1(main_2_rd1), .RD2(main_2_rd2), .WE3(RegWrite), .CLK(CLK));
  ALU_main main_3 (
    .A(main_2_rd1), .B(main_2_rd2), .ALUOutput(main_3_aluoutput), .Negative(main_3_negative),
    .Zero(main_3_zero), .ALUControl(ALUControl));
  not not_1 (not_1_out, main_3_zero);
  RAM #(.addrWidth(16), .dataWidth(16), .bus("separate")) ram_1 (
    .addr(rom_1_data), .din(main_2_rd1), .data(ram_1_data), .str(MemWrite), .sel(1'b1), .clk(CLK), .ld(1'b1),
    .clr(in_2));
  and and_1 (and_1_out, not_1_out, not_2_out);
  not not_2 (not_2_out, main_3_negative);
  Multiplexer #(.select(2), .width(16), .enable("false")) multiplexer_5 (
    .in0(main_3_aluoutput), .in1(rom_1_data), .in2(ram_1_data), .out(multiplexer_5_out), .sel(WD3Select));  // open: in3
  Multiplexer #(.select(2), .enable("false")) multiplexer_6 (
    .in0(main_3_zero), .in1(not_1_out), .in2(and_1_out), .in3(main_3_negative), .out(multiplexer_6_out),
    .sel(BrSelect));

  // Notes on the sheet:
  //   contents of rom_1 (hex, n*v repeats v):
  //   2200041 2400071 246000 2500081 2700051 578001 2a00031 18affa0
  //   Data Memory
endmodule
